// Logisim project Experiment 1.1 (221B312).circ as structural Verilog: 1 circuit, main circuit main
module main (
  input  a,
  input  b,
  output x,
  output y,
  output z,
  output u,
  output v
);

  wire and_2_out, and_3_out, not_2_out, not_3_out, not_4_out, not_5_out;

  not not_1 (x, b);
  and and_1 (y, a, b);
  or or_1 (z, b, a);
  not not_2 (not_2_out, a);
  not not_3 (not_3_out, b);
  not not_4 (not_4_out, a);
  not not_5 (not_5_out, b);
  or or_2 (u, not_2_out, not_3_out);
  and and_2 (and_2_out, not_4_out, b);
  and and_3 (and_3_out, a, not_5_out);
  or or_3 (v, and_2_out, and_3_out);
endmodule
