// Logisim project Experiment 1.3 (221b312).circ as structural Verilog: 2 circuits, main circuit main
module main (
  input  X,
  input  Y,
  input  Z,
  output OUTPUT
);

  wire and_1_out, and_2_out, and_3_out;

  and and_1 (and_1_out, X, Y);
  and and_2 (and_2_out, Y, Z);
  and and_3 (and_3_out, Z, X);
  or or_1 (OUTPUT, and_1_out, and_2_out, and_3_out);

  // Notes on the sheet:
  //   INPUT
  //   Experiment 1.3
  //   221b312
endmodule

module Experiment_1_3 (
  input  a,
  input  b,
  input  c,
  output x
);

  wire and_1_out, and_2_out, and_3_out;

  and and_1 (and_1_out, b, c);
  and and_2 (and_2_out, a, c);
  and and_3 (and_3_out, a, b);
  or or_1 (x, and_1_out, and_2_out, and_3_out);
endmodule
