// Logisim project Lab 1- gates implementation.circ as structural Verilog: 1 circuit, main circuit main
module main (
  input  in_1,
  input  in_2,
  input  in_3,
  input  in_4,
  input  in_5,
  input  in_6,
  input  in_7,
  input  in_8,
  input  in_9,
  input  in_10,
  input  in_11,
  input  in_12,
  input  in_13,
  input  in_14,
  input  in_15,
  input  in_16,
  input  in_17,
  input  in_18,
  input  in_19,
  input  in_20,
  input  in_21,
  input  in_22,
  output out_23,
  output out_24,
  output out_25,
  output out_26,
  output out_27,
  output out_28,
  output out_29,
  output out_30,
  output out_31,
  output out_32,
  output out_33,
  output out_34
);

  not not_1 (out_23, in_3);
  and and_1 (out_27, in_7, in_10);
  or or_1 (out_29, in_12, in_14);
  buf buffer_1 (out_33, in_19);
  nand nand_1 (out_24, in_1, in_4);
  nor nor_1 (out_28, in_8, in_11);
  xor xor_1 (out_30, in_13, in_16);
  xnor xnor_1 (out_32, in_18, in_20);
  assign out_34 = in_22 ? ~in_21 : 1'bz;  // Controlled_Inverter controlled_inverter_1
  xor odd_parity_1 (out_25, in_2, in_5);
  xnor even_parity_1 (out_26, in_6, in_9);
  assign out_31 = in_17 ? in_15 : 1'bz;  // Controlled_Buffer controlled_buffer_1
endmodule
