// Logisim project 4 Bit binary adder.circ as structural Verilog: 1 circuit, main circuit main
module main (
  input  in_1,
  input  [3:0] in_2,
  input  [3:0] in_3,
  output out_4,
  output out_5,
  output out_6,
  output out_7
);

  wire adder_1_cout, adder_2_cout, adder_3_cout, xor_1_out, xor_2_out, xor_3_out, xor_4_out;
  wire [0:0] adder_1_out;

  Hex_Digit_Display hex_digit_display_1 (.value(in_2));  // open: dp
  Hex_Digit_Display hex_digit_display_2 (.value(in_3));  // open: dp
  xor xor_1 (xor_1_out, in_1, in_3[0]);
  xor xor_2 (xor_2_out, in_1, in_3[1]);
  xor xor_3 (xor_3_out, in_1, in_3[2]);
  xor xor_4 (xor_4_out, in_1, in_3[3]);
  Adder #(.width(1)) adder_1 (.a(in_2[0]), .b(xor_1_out), .out(adder_1_out[0]), .cin(in_1), .cout(adder_1_cout));
  Adder #(.width(1)) adder_2 (.a(in_2[1]), .b(xor_2_out), .out(out_4), .cin(adder_1_cout), .cout(adder_2_cout));
  Adder #(.width(1)) adder_3 (.a(in_2[2]), .b(xor_3_out), .out(out_5), .cin(adder_2_cout), .cout(adder_3_cout));
  Adder #(.width(1)) adder_4 (.a(in_2[3]), .b(xor_4_out), .out(out_6), .cin(adder_3_cout), .cout(out_7));
  Hex_Digit_Display hex_digit_display_3 (.value({3'b000, out_7}));  // open: dp
  Hex_Digit_Display hex_digit_display_4 (.value({out_6, out_5, out_4, adder_1_out[0]}));  // open: dp

  // Notes on the sheet:
  //   4 Bit Binary Adder(221B069)
endmodule
