// Logisim project Experiment 1.2 (221B312).circ as structural Verilog: 2 circuits, main circuit main
module main (
  input  a,
  input  b,
  input  c,
  input  d,
  output x
);

  wire and_1_out, and_2_out, and_3_out, and_4_out, not_1_out, not_2_out, not_3_out, not_4_out, not_5_out;

  not not_1 (not_1_out, b);
  and and_1 (and_1_out, not_1_out, c, d);
  and and_2 (and_2_out, b, not_2_out, not_3_out);
  not not_2 (not_2_out, c);
  not not_3 (not_3_out, d);
  and and_3 (and_3_out, a, not_4_out, d);
  not not_4 (not_4_out, c);
  and and_4 (and_4_out, a, c, not_5_out);
  not not_5 (not_5_out, d);
  or or_1 (x, and_1_out, and_2_out, and_3_out, and_4_out);

  // Notes on the sheet:
  //   Experiment 1.2
  //   221b312
endmodule

module Experiment_1_two (
  input  a,
  input  b,
  input  c,
  input  d,
  output x
);

  wire and_1_out, and_2_out, and_3_out, and_4_out, not_1_out, not_2_out, not_3_out, not_4_out, not_5_out;

  not not_1 (not_1_out, b);
  and and_1 (and_1_out, not_1_out, c, d);
  and and_2 (and_2_out, b, not_2_out, not_3_out);
  not not_2 (not_2_out, c);
  not not_3 (not_3_out, d);
  and and_3 (and_3_out, a, not_4_out, d);
  not not_4 (not_4_out, c);
  and and_4 (and_4_out, a, c, not_5_out);
  not not_5 (not_5_out, d);
  or or_1 (x, and_1_out, and_2_out, and_3_out, and_4_out);
endmodule
