// Logisim project Experiment 1.4 (221b312).circ as structural Verilog: 1 circuit, main circuit main
module main (
  input  A,
  input  B,
  input  C,
  output out_4
);

  wire and_1_out, and_2_out, and_3_out, not_1_out, not_3_out, or_1_out, xor_1_out;

  not not_1 (not_1_out, A);
  // NOT_Gate not_2 has open pins: in=B, out=open
  not not_3 (not_3_out, C);
  xor xor_1 (xor_1_out, A, B);
  and and_1 (and_1_out, A, B);
  and and_2 (and_2_out, B, C);
  and and_3 (and_3_out, A, C);
  // XOR_Gate xor_2 has open pins: in0=xor_1_out, in1=C, out=open
  or or_1 (or_1_out, and_1_out, and_2_out, and_3_out);
  or or_2 (out_4, or_1_out, not_3_out);

  // Notes on the sheet:
  //   Experiment 1.4
  //   221b312
endmodule
