// Logisim project Half Sub.circ as structural Verilog: 1 circuit, main circuit main
module main (
  input  A,
  input  B,
  output X,
  output Y
);

  wire not_1_out;

  xor DIFF (X, A, B);
  not not_1 (not_1_out, A);
  and BORROW (Y, not_1_out, B);

  // Notes on the sheet:
  //   Half Subtracter(221B069)
endmodule
