// Logisim project RIPPLE CARRY ADDER.circ as structural Verilog: 3 circuits, main circuit HALF ADDER
module HALF_ADDER (
  input  A,
  input  B,
  output sum,
  output carry
);

  xor XOR (sum, A, B);
  and AND (carry, A, B);
endmodule

module FA (
  input  A,
  input  B,
  input  CIN,
  output SUM,
  output CARRY
);

  wire HA_2_carry, HA_carry, HA_sum;

  HALF_ADDER HA (.A(A), .B(B), .sum(HA_sum), .carry(HA_carry));
  HALF_ADDER HA_2 (.A(HA_sum), .B(CIN), .sum(SUM), .carry(HA_2_carry));
  or OR (CARRY, HA_2_carry, HA_carry);
endmodule

module Ripple_Carry_Adder (
  input  [3:0] in_1,
  input  [3:0] in_2,
  output out_3
);

  wire FA_2_carry, FA_carry, HA_carry;
  wire [3:0] HA_sum;

  Hex_Digit_Display hex_digit_display_1 (.value(in_1));  // open: dp
  Hex_Digit_Display hex_digit_display_2 (.value(in_2));  // open: dp
  HALF_ADDER HA (.A(in_1[0]), .B(in_2[0]), .sum(HA_sum[0]), .carry(HA_carry));
  FA FA (.A(HA_carry), .B(in_1[1]), .CIN(in_2[1]), .SUM(HA_sum[1]), .CARRY(FA_carry));
  FA FA_2 (.A(FA_carry), .B(in_1[2]), .CIN(in_2[2]), .SUM(HA_sum[2]), .CARRY(FA_2_carry));
  FA FA_3 (.A(FA_2_carry), .B(in_1[3]), .CIN(in_2[3]), .SUM(HA_sum[3]), .CARRY(out_3));
  Hex_Digit_Display hex_digit_display_3 (.value({3'b000, out_3}));  // open: dp
  Hex_Digit_Display hex_digit_display_4 (.value(HA_sum));  // open: dp
endmodule
