// Logisim project experiemnt 1.1 (221b312).circ as structural Verilog: 1 circuit, main circuit main
module main (
  input  A,
  input  B,
  output Sum,
  output Carry
);

  xor xor_1 (Sum, A, B);
  and and_1 (Carry, A, B);

  // Notes on the sheet:
  //   Experiment 1.1
  //   Half Adder
  //   221b312
endmodule
