// Logisim project experiemnt 1.2 (221b312).circ as structural Verilog: 1 circuit, main circuit main
module main (
  input  A,
  input  B,
  output Sum,
  output Carry
);

  wire not_1_out;

  not not_1 (not_1_out, A);
  xor xor_1 (Sum, A, B);
  and and_1 (Carry, B, not_1_out);

  // Notes on the sheet:
  //   Experiemnt 1.2
  //   221b312
  //   Half Subractor
endmodule
