// Logisim project experiment 2.2(without adding circuit) (221b312).circ as structural Verilog: 1 circuit, main circuit main
module main (
  input  A,
  input  B,
  input  C,
  output difference,
  output borrow
);

  wire and_1_out, and_2_out, not_1_out, not_2_out, xor_1_out;

  not not_1 (not_1_out, B);
  xor xor_1 (xor_1_out, B, C);
  and and_1 (and_1_out, C, not_1_out);
  not not_2 (not_2_out, A);
  xor xor_2 (difference, A, xor_1_out);
  and and_2 (and_2_out, xor_1_out, not_2_out);
  or or_1 (borrow, and_2_out, and_1_out);

  // Notes on the sheet:
  //   Experiment  2.2
  //   221b312
  //   Full Subtractor
endmodule
