// Logisim project experiment 3 (221b312).circ as structural Verilog: 3 circuits, main circuit main
module main (
  input  [3:0] in_1,
  input  [3:0] in_2,
  output S0,
  output S1,
  output S2,
  output S3,
  output C3
);

  wire fa_1_carry, fa_2_carry, ha_1_carry;

  Hex_Digit_Display hex_digit_display_1 ();  // open: value, dp
  Hex_Digit_Display hex_digit_display_2 ();  // open: value, dp
  HA ha_1 (.A(in_1[0]), .B(in_2[0]), .Sum(S0), .Carry(ha_1_carry));
  FA fa_1 (.A(in_1[1]), .B(in_2[1]), .C(ha_1_carry), .Sum(S1), .Carry(fa_1_carry));
  FA fa_2 (.A(in_1[2]), .B(in_2[2]), .C(fa_1_carry), .Sum(S2), .Carry(fa_2_carry));
  FA fa_3 (.A(in_1[3]), .B(in_2[3]), .C(fa_2_carry), .Sum(S3), .Carry(C3));

  // Notes on the sheet:
  //   Experiment 3
  //   221b312
  //   4-bit binary adder
  //   C0
  //   C1
  //   C2
endmodule

module HA (
  input  A,
  input  B,
  output Sum,
  output Carry
);

  xor xor_1 (Sum, A, B);
  and and_1 (Carry, A, B);

  // Notes on the sheet:
  //   Experiment 1.1
  //   Half Adder
  //   221b312
endmodule

module FA (
  input  A,
  input  B,
  input  C,
  output Sum,
  output Carry
);

  wire and_1_out, and_2_out, xor_1_out;

  xor xor_1 (xor_1_out, A, B);
  xor xor_2 (Sum, xor_1_out, C);
  and and_1 (and_1_out, xor_1_out, C);
  and and_2 (and_2_out, A, B);
  or or_1 (Carry, and_1_out, and_2_out);

  // Notes on the sheet:
  //   Experiment 1.1
  //   221b312
  //   Full Adder
endmodule
