// Logisim project experiment 4 (221b312).circ as structural Verilog: 3 circuits, main circuit main
module main (
  input  C0,
  input  [3:0] in_2,
  output S1,
  output S2,
  output S3,
  output S4,
  output C4
);

  wire fa_1_carry, fa_2_carry, fa_3_carry, xor_1_out, xor_2_out, xor_3_out, xor_4_out;
  wire [3:0] undriven;

  Hex_Digit_Display hex_digit_display_1 ();  // open: value, dp
  Hex_Digit_Display hex_digit_display_2 ();  // open: value, dp
  xor xor_1 (xor_1_out, undriven[0], C0);
  xor xor_2 (xor_2_out, undriven[1], C0);
  xor xor_3 (xor_3_out, undriven[2], C0);
  xor xor_4 (xor_4_out, undriven[3], C0);
  FA fa_1 (.A(C0), .B(in_2[0]), .C(xor_1_out), .Sum(S1), .Carry(fa_1_carry));
  FA fa_2 (.A(fa_1_carry), .B(in_2[1]), .C(xor_2_out), .Sum(S2), .Carry(fa_2_carry));
  FA fa_3 (.A(fa_2_carry), .B(in_2[2]), .C(xor_3_out), .Sum(S3), .Carry(fa_3_carry));
  FA fa_4 (.A(fa_3_carry), .B(in_2[3]), .C(xor_4_out), .Sum(S4), .Carry(C4));

  // Notes on the sheet:
  //   Experiement 4
  //   221b312
  //   4-bit binary adder-subtractor
endmodule

module FA (
  input  A,
  input  B,
  input  C,
  output Sum,
  output Carry
);

  wire and_1_out, and_2_out, xor_1_out;

  xor xor_1 (xor_1_out, A, B);
  xor xor_2 (Sum, xor_1_out, C);
  and and_1 (and_1_out, xor_1_out, C);
  and and_2 (and_2_out, A, B);
  or or_1 (Carry, and_1_out, and_2_out);

  // Notes on the sheet:
  //   Experiment 1.1
  //   221b312
  //   Full Adder
endmodule

module HA (
  input  A,
  input  B,
  output Sum,
  output Carry
);

  xor xor_1 (Sum, A, B);
  and and_1 (Carry, A, B);

  // Notes on the sheet:
  //   Experiment 1.1
  //   Half Adder
  //   221b312
endmodule
