// Logisim project 1.3 (8X1 multiplexer) (221b312).circ as structural Verilog: 4 circuits, main circuit main
module main (
  input  I0,
  input  I1,
  input  I2,
  input  I3,
  input  S2,
  input  S0,
  input  S1,
  input  I4,
  input  I5,
  input  I6,
  input  I7,
  output out_12
);

  wire n4x1_1_out_7, n4x1_2_out_7;

  _4x1 u_4x1_1 (.I0(I0), .I1(I1), .I2(I2), .I3(I3), .S1(S0), .S0(S1), .out_7(n4x1_1_out_7));
  _4x1 u_4x1_2 (.I0(I4), .I1(I5), .I2(I6), .I3(I7), .S1(S0), .S0(S1), .out_7(n4x1_2_out_7));
  _2x1 u_2x1_1 (.I0(n4x1_1_out_7), .S(S2), .I1(n4x1_2_out_7), .Y(out_12));

  // Notes on the sheet:
  //   8x1 multiplexer
  //   221b312
endmodule

module _2x1 (
  input  I0,
  input  S,
  input  I1,
  output Y
);

  wire and_1_out, and_2_out, not_1_out;

  not not_1 (not_1_out, S);
  and and_1 (and_1_out, I0, not_1_out);
  and and_2 (and_2_out, I1, S);
  or or_1 (Y, and_1_out, and_2_out);

  // Notes on the sheet:
  //   SI1
  //   S'I0
endmodule

module _4x1 (
  input  I0,
  input  I1,
  input  I2,
  input  I3,
  input  S0,
  input  S1,
  output out_7
);

  wire n2x1_1_y, n2x1_2_y;

  _2x1 u_2x1_1 (.I0(I0), .S(S0), .I1(I1), .Y(n2x1_1_y));
  _2x1 u_2x1_2 (.I0(I2), .S(S0), .I1(I3), .Y(n2x1_2_y));
  _2x1 u_2x1_3 (.I0(n2x1_1_y), .S(S1), .I1(n2x1_2_y), .Y(out_7));

  // Notes on the sheet:
  //   4x1 multiplexer
  //   221b312
endmodule

module _8X1 (
  input  I0,
  input  I1,
  input  I2,
  input  I3,
  input  S2,
  input  S0,
  input  S1,
  input  I4,
  input  I5,
  input  I6,
  input  I7,
  output out_12
);

  wire n4x1_1_out_7, n4x1_2_out_7;

  _4x1 u_4x1_1 (.I0(I0), .I1(I1), .I2(I2), .I3(I3), .S1(S0), .S0(S1), .out_7(n4x1_1_out_7));
  _4x1 u_4x1_2 (.I0(I4), .I1(I5), .I2(I6), .I3(I7), .S1(S0), .S0(S1), .out_7(n4x1_2_out_7));
  _2x1 u_2x1_1 (.I0(n4x1_1_out_7), .S(S2), .I1(n4x1_2_out_7), .Y(out_12));
endmodule
