// Logisim project 2.1 (1x2 demultiplexer) (221b312).circ as structural Verilog: 1 circuit, main circuit main
module main (
  input  Y,
  input  S0,
  input  S1,
  output I0,
  output out_5
);

  Demultiplexer demultiplexer_1 (.out0(I0), .out1(out_5), .in(Y), .sel(S1), .en(S0));

  // Notes on the sheet:
  //   1x2 demultiplexer
  //   221b312
endmodule
