// Logisim project 2.2 (1x4 demultiplexer) (221b312).circ as structural Verilog: 1 circuit, main circuit main
module main (
  input  Y,
  input  S0,
  input  S1,
  output I0,
  output I1,
  output I2,
  output I3
);

  Demultiplexer demultiplexer_1 (.out0(I1), .out1(I3), .in(Y), .sel(S1), .en(S0));
endmodule
