// Logisim project 3 (221b312).circ as structural Verilog: 1 circuit, main circuit main
module main (
);

  wire [3:1] undriven, undriven_2;
  wire [3:3] or_1_out, or_2_out;

  _7_Segment_Display u_7_segment_display_1 ();  // open: g, f, a, b, e, d, c, dp
  _7_Segment_Display u_7_segment_display_2 ();  // open: g, f, a, b, e, d, c, dp
  // OR_Gate or_1 has open pins: out=or_1_out[3]
  // OR_Gate or_2 has open pins: out=or_2_out[3]
  Hex_Digit_Display hex_digit_display_1 (.value({undriven, or_1_out[3]}));  // open: dp
  Hex_Digit_Display hex_digit_display_2 (.value({undriven_2, or_2_out[3]}));  // open: dp
  // Pins of 1 and 4 bits meet at {undriven, or_1_out[3]}
  // Pins of 1 and 4 bits meet at {4{or_1_out[3]}}
  // Pins of 1 and 4 bits meet at {4{or_2_out[3]}}
  // Pins of 1 and 4 bits meet at {undriven_2, or_2_out[3]}
endmodule
