// Logisim project q1.circ as structural Verilog: 3 circuits, main circuit 8x1Mux
module _2x1Mux (
  input  i0,
  input  i1,
  input  s,
  output y
);

  wire and_1_out, and_2_out, not_1_out;

  not not_1 (not_1_out, s);
  and and_1 (and_1_out, i0, not_1_out);
  and and_2 (and_2_out, i1, s);
  or or_1 (y, and_1_out, and_2_out);

  // Notes on the sheet:
  //   221b307
  //   2x1
endmodule

module _4x1Mux (
  input  i0,
  input  i1,
  input  i2,
  input  i3,
  input  s0,
  input  s1,
  output Output
);

  wire n2x1mux_1_y, n2x1mux_2_y;

  _2x1Mux u_2x1mux_1 (.i0(i0), .i1(i1), .s(s0), .y(n2x1mux_1_y));
  _2x1Mux u_2x1mux_2 (.i0(i2), .i1(i3), .s(s0), .y(n2x1mux_2_y));
  _2x1Mux u_2x1mux_3 (.i0(n2x1mux_1_y), .i1(n2x1mux_2_y), .s(s1), .y(Output));

  // Notes on the sheet:
  //   221b307
endmodule

module _8x1Mux (
  input  i0,
  input  i1,
  input  i2,
  input  i3,
  input  i4,
  input  i5,
  input  i6,
  input  i7,
  input  s0,
  input  s1,
  input  s2,
  output \output 
);

  wire n4x1mux_1_output, n4x1mux_2_output;

  _4x1Mux u_4x1mux_1 (.i0(i0), .i1(i1), .i2(i2), .i3(i3), .s0(s0), .s1(s1), .Output(n4x1mux_1_output));
  _4x1Mux u_4x1mux_2 (.i0(i4), .i1(i5), .i2(i6), .i3(i7), .s0(s0), .s1(s1), .Output(n4x1mux_2_output));
  _2x1Mux u_2x1mux_1 (.i0(n4x1mux_1_output), .i1(n4x1mux_2_output), .s(s2), .y(\output ));

  // Notes on the sheet:
  //   8 x 1 Mux
  //   221b307
endmodule
