// Logisim project q2.circ as structural Verilog: 4 circuits, main circuit 1x8 using 3 1x4
module _1x4_Dmux (
  input  \input ,
  input  enable,
  input  [1:0] select,
  output o0,
  output o1,
  output o2,
  output o3
);

  Demultiplexer #(.select(2)) demultiplexer_1 (
    .out0(o0), .out1(o1), .out2(o2), .out3(o3), .in(\input ), .sel(select), .en(enable));
endmodule

module _1x8_Dmux (
  input  in_1,
  input  enable,
  input  s0,
  input  [1:0] s1_and_s2,
  output o0,
  output o1,
  output o2,
  output o3,
  output o4,
  output o5,
  output o6,
  output o
);

  wire n1x2_dmux_1_o0, n1x2_dmux_1_o1;

  _1x2_Dmux u_1x2_dmux_1 (.\input (in_1), .select(enable), .o0(n1x2_dmux_1_o0), .o1(n1x2_dmux_1_o1));
  _1x4_Dmux u_1x4_dmux_1 (
    .\input (n1x2_dmux_1_o0), .enable(enable), .select(s1_and_s2), .o0(o0), .o1(o1), .o2(o2), .o3(o3));
  _1x4_Dmux u_1x4_dmux_2 (
    .\input (n1x2_dmux_1_o1), .enable(enable), .select(s1_and_s2), .o0(o4), .o1(o5), .o2(o6), .o3(o));
endmodule

module _1x2_Dmux (
  input  \input ,
  input  select,
  output o0,
  output o1
);

  Demultiplexer #(.enable("false")) demultiplexer_1 (.out0(o0), .out1(o1), .in(\input ), .sel(select));
endmodule

module _1x8_using_3_1x4 (
  input  \input ,
  input  enable,
  input  [1:0] s0,
  input  [1:0] s1_and_s2,
  output o0,
  output o1,
  output o2,
  output o3,
  output o4,
  output o5,
  output o6,
  output o
);

  wire n1x4_dmux_1_o0, n1x4_dmux_1_o1, n1x4_dmux_1_o2;

  _1x4_Dmux u_1x4_dmux_1 (
    .\input (\input ), .enable(enable), .select(s0), .o0(n1x4_dmux_1_o0), .o1(n1x4_dmux_1_o1),
    .o2(n1x4_dmux_1_o2), .o3(n1x4_dmux_1_o2));
  _1x4_Dmux u_1x4_dmux_2 (
    .\input (n1x4_dmux_1_o0), .enable(enable), .select(s1_and_s2), .o0(o0), .o1(o1), .o2(o2), .o3(o3));
  _1x4_Dmux u_1x4_dmux_3 (
    .\input (n1x4_dmux_1_o1), .enable(enable), .select(s1_and_s2), .o0(o4), .o1(o5), .o2(o6), .o3(o));
  // also tied to GND on the sheet: n1x4_dmux_1_o2

  // Notes on the sheet:
  //   221b307
endmodule
