// Logisim project q3.circ as structural Verilog: 1 circuit, main circuit main
module main (
  input  i3,
  input  i2,
  input  i1,
  input  i0,
  output o1,
  output o0
);

  _7_Segment_Display u_7_segment_display_1 (.g(i3), .a(i3), .b(i3), .d(i3), .c(i3));  // open: f, e, dp
  _7_Segment_Display u_7_segment_display_2 (.g(i2), .a(i2), .b(i2), .e(i2), .d(i2));  // open: f, c, dp
  _7_Segment_Display u_7_segment_display_3 (.b(i1), .c(i1));  // open: g, f, a, e, d, dp
  _7_Segment_Display u_7_segment_display_4 (.f(i0), .a(i0), .b(i0), .e(i0), .d(i0), .c(i0));  // open: g, dp
  or or_1 (o1, i3, i2);
  or or_2 (o0, i1, i3);
  Hex_Digit_Display hex_digit_display_1 (.value({3'b000, o1}));  // open: dp
  Hex_Digit_Display hex_digit_display_2 (.value({3'b000, o0}));  // open: dp
endmodule
