// Logisim project q4.circ as structural Verilog: 2 circuits, main circuit 3_to_8_decoder
module _2_to_4_decoder (
  input  in_1,
  input  [1:0] in_2,
  output out_3,
  output out_4,
  output out_5,
  output out_6
);

  Decoder #(.select(2)) decoder_1 (.out0(out_3), .out1(out_4), .out2(out_5), .out3(out_6), .sel(in_2), .en(in_1));
endmodule

module _3_to_8_decoder (
  input  [1:0] a0___a1,
  input  enable,
  output i0,
  output i1,
  output i2,
  output i3,
  output i4,
  output i5,
  output i6,
  output i7
);

  wire not_1_out;

  not not_1 (not_1_out, enable);
  _2_to_4_decoder u_2_to_4_decoder_1 (.in_1(not_1_out), .in_2(a0___a1), .out_3(i0), .out_4(i1), .out_5(i2), .out_6(i3));
  _2_to_4_decoder u_2_to_4_decoder_2 (.in_1(enable), .in_2(a0___a1), .out_3(i4), .out_4(i5), .out_5(i6), .out_6(i7));

  // Notes on the sheet:
  //   221b307
endmodule
