// Logisim project experiment 2.1 (221b312).circ as structural Verilog: 1 circuit, main circuit main
module main (
  input  A,
  input  B,
  input  C,
  output Sum,
  output Carry
);

  wire and_1_out, and_2_out, xor_1_out;

  xor xor_1 (xor_1_out, A, B);
  xor xor_2 (Sum, xor_1_out, C);
  and and_1 (and_1_out, xor_1_out, C);
  and and_2 (and_2_out, A, B);
  or or_1 (Carry, and_1_out, and_2_out);

  // Notes on the sheet:
  //   Experiment 1.1
  //   221b312
  //   Full Adder
endmodule
