// Logisim project experiment 2.2 (221b312).circ as structural Verilog: 3 circuits, main circuit main
module main (
  input  A,
  input  B,
  input  C,
  output Difference,
  output Borrow
);

  wire hs_1_carry, hs_1_sum, hs_2_carry;

  HS hs_1 (.A(B), .B(C), .Sum(hs_1_sum), .Carry(hs_1_carry));
  HS hs_2 (.A(A), .B(hs_1_sum), .Sum(Difference), .Carry(hs_2_carry));
  or or_1 (Borrow, hs_2_carry, hs_1_carry);

  // Notes on the sheet:
  //   Experiment 1.1
  //   Full Subtractor
  //   221b312
endmodule

module HA (
  input  A,
  input  B,
  output Sum,
  output Carry
);

  xor xor_1 (Sum, A, B);
  and and_1 (Carry, A, B);
endmodule

module HS (
  input  A,
  input  B,
  output Sum,
  output Carry
);

  wire not_1_out;

  not not_1 (not_1_out, A);
  xor xor_1 (Sum, A, B);
  and and_1 (Carry, B, not_1_out);

  // Notes on the sheet:
  //   Experiemnt 1.2
  //   221b312
  //   Half Subractor
endmodule
