// Logisim project 1.1 (full adder using in-built blockr) (221b312).circ as structural Verilog: 3 circuits, main circuit main
// S1
module main (
  input  I0,
  input  I1,
  input  I2,
  input  I3,
  input  S0,
  input  S1,
  output out_7
);

  wire n2x1_1_y, n2x1_2_y;

  _2x1 u_2x1_1 (.I0(I0), .S(S0), .I1(I1), .Y(n2x1_1_y));
  _2x1 u_2x1_2 (.I0(I2), .S(S0), .I1(I3), .Y(n2x1_2_y));
  _2x1 u_2x1_3 (.I0(n2x1_1_y), .S(S1), .I1(n2x1_2_y), .Y(out_7));

  // Notes on the sheet:
  //   4x1 multiplexer
  //   221b312
endmodule

module _2x1 (
  input  I0,
  input  S,
  input  I1,
  output Y
);

  wire and_1_out, and_2_out, not_1_out;

  not not_1 (not_1_out, S);
  and and_1 (and_1_out, I0, not_1_out);
  and and_2 (and_2_out, I1, S);
  or or_1 (Y, and_1_out, and_2_out);

  // Notes on the sheet:
  //   SI1
  //   S'I0
endmodule

module full_adder_using_in_built_block (
  input  A,
  input  B,
  input  C,
  output out_4
);

  wire n2x1_1_y, n2x1_2_y, not_1_out;

  not not_1 (not_1_out, A);
  _2x1 u_2x1_1 (.I0(A), .S(B), .I1(not_1_out), .Y(n2x1_1_y));
  _2x1 u_2x1_2 (.I0(not_1_out), .S(B), .I1(A), .Y(n2x1_2_y));
  _2x1 u_2x1_3 (.I0(n2x1_1_y), .S(C), .I1(n2x1_2_y), .Y(out_4));
endmodule
