// Logisim project 1.2 (full adder using in-built block USING 8X1) (221b312).circ as structural Verilog: 1 circuit, main circuit main
module main (
  input  [7:0] in_1,
  input  [7:0] in_2,
  input  [2:0] in_3,
  input  [2:0] in_4,
  output out_5,
  output out_6
);

  wire [2:1] multiplexer_1_out, undriven, undriven_2, undriven_3, undriven_4, undriven_5, undriven_6,
       undriven_7, undriven_8;
  wire [7:1] multiplexer_2_out, undriven_9, undriven_10, undriven_11, undriven_12, undriven_13, undriven_14,
       undriven_15, undriven_16;

  Multiplexer #(.select(3), .width(3)) multiplexer_1 (
    .in0({undriven, in_1[0]}), .in1({undriven_2, in_1[1]}), .in2({undriven_3, in_1[2]}),
    .in3({undriven_4, in_1[3]}), .in4({undriven_5, in_1[4]}), .in5({undriven_6, in_1[5]}),
    .in6({undriven_7, in_1[6]}), .in7({undriven_8, in_1[7]}), .out({multiplexer_1_out, out_5}), .sel(in_3),
    .en(in_4[0]));
  Multiplexer #(.select(3), .width(8)) multiplexer_2 (
    .in0({undriven_9, in_2[0]}), .in1({undriven_10, in_2[1]}), .in2({undriven_11, in_2[2]}),
    .in3({undriven_12, in_2[3]}), .in4({undriven_13, in_2[4]}), .in5({undriven_14, in_2[5]}),
    .in6({undriven_15, in_2[6]}), .in7({undriven_16, in_2[7]}), .out({multiplexer_2_out, out_6}), .sel(in_3),
    .en(in_4[0]));
  // Pins of 1 and 3 bits meet at in_4
  // Pins of 1 and 3 bits meet at {multiplexer_1_out, out_5}
  // Pins of 1 and 8 bits meet at {multiplexer_2_out, out_6}
  // Pins of 1 and 8 bits meet at {undriven_9, in_2[0]}
  // Pins of 1 and 8 bits meet at {undriven_10, in_2[1]}
  // Pins of 1 and 8 bits meet at {undriven_11, in_2[2]}
  // Pins of 1 and 8 bits meet at {undriven_12, in_2[3]}
  // Pins of 1 and 8 bits meet at {undriven_13, in_2[4]}
  // Pins of 1 and 8 bits meet at {undriven_14, in_2[5]}
  // Pins of 1 and 8 bits meet at {undriven_15, in_2[6]}
  // Pins of 1 and 8 bits meet at {undriven_16, in_2[7]}
  // Pins of 1 and 3 bits meet at {undriven, in_1[0]}
endmodule
