// Logisim project 2 (priority encoder) (221b312).circ as structural Verilog: 1 circuit, main circuit main
module main (
  input  in_1,
  input  in_2,
  input  in_3,
  input  in_4,
  output out_5,
  output out_6,
  output out_7
);

  wire and_1_out, not_1_out;

  Hex_Digit_Display hex_digit_display_1 ();  // open: value, dp
  not not_1 (not_1_out, in_2);
  and and_1 (and_1_out, not_1_out, in_3);
  or or_1 (out_5, in_1, and_1_out);
  or or_2 (out_6, in_1, in_3);
  or or_3 (out_7, in_1, not_1_out, in_3, in_4);
  _7_Segment_Display u_7_segment_display_1 ();  // open: g, f, a, b, e, d, c, dp
endmodule
