// Logisim project 3 calendar logic circuit (221B312).circ as structural Verilog: 1 circuit, main circuit main
module main (
  input  L,
  input  M0,
  input  M1,
  input  M2,
  input  M3,
  output D28,
  output D29,
  output D30,
  output D31
);

  wire and_3_out, and_4_out, not_1_out, not_2_out, not_3_out, not_4_out, not_5_out;

  Hex_Digit_Display hex_digit_display_1 (.value({M3, M2, M1, M0}));  // open: dp
  not not_1 (not_1_out, L);
  not not_2 (not_2_out, M0);
  not not_3 (not_3_out, M1);
  not not_4 (not_4_out, M2);
  not not_5 (not_5_out, M3);
  and and_1 (D28, not_1_out, not_2_out, M1, not_4_out, not_5_out);
  and and_2 (D29, L, M0, not_3_out, not_4_out, not_5_out);
  and and_3 (and_3_out, M0, not_5_out);
  and and_4 (and_4_out, not_2_out, M2, not_5_out);
  _7_Segment_Display u_7_segment_display_1 (.g(D28), .f(D28), .a(D28), .b(D28), .e(D28), .d(D28), .c(D28), .dp(D28));
  xor xor_1 (D31, M0, M3);
  _7_Segment_Display u_7_segment_display_2 (.g(D28), .f(D28), .a(D28), .b(D28), .e(D28), .d(D28), .c(D28), .dp(D28));
  _7_Segment_Display u_7_segment_display_3 (.g(D29), .f(D29), .a(D29), .b(D29), .e(D29), .d(D29), .c(D29), .dp(D29));
  or or_1 (D30, and_3_out, and_4_out);
  _7_Segment_Display u_7_segment_display_4 (.g(D29), .f(D29), .a(D29), .b(D29), .e(D29), .d(D29), .c(D29), .dp(D29));
  _7_Segment_Display u_7_segment_display_5 (.g(D30), .f(D30), .a(D30), .b(D30), .e(D30), .d(D30), .c(D30), .dp(D30));
  _7_Segment_Display u_7_segment_display_6 (.g(D30), .f(D30), .a(D30), .b(D30), .e(D30), .d(D30), .c(D30), .dp(D30));
  _7_Segment_Display u_7_segment_display_7 (.g(D31), .f(D31), .a(D31), .b(D31), .e(D31), .d(D31), .c(D31), .dp(D31));
  _7_Segment_Display u_7_segment_display_8 (.g(D31), .f(D31), .a(D31), .b(D31), .e(D31), .d(D31), .c(D31), .dp(D31));
endmodule
