// Logisim project 4 (input year is leap year or not.) (221B312).circ as structural Verilog: 1 circuit, main circuit main
module main (
  input  in_1,
  input  [3:0] Y0,
  input  in_3,
  input  in_4,
  input  in_5,
  input  [3:0] YT,
  input  in_7,
  input  in_8,
  input  in_9,
  input  in_10,
  input  in_11,
  input  [3:0] YH,
  input  in_13,
  input  in_14,
  input  in_15,
  input  [3:0] YTH,
  input  in_17,
  input  in_18,
  input  in_19,
  input  in_20,
  output out_21,
  output out_22,
  output out_23,
  output out_24
);

  wire [3:2] undriven;

  Hex_Digit_Display hex_digit_display_1 (.value({in_5, in_4, in_3, in_1}));  // open: dp
  Hex_Digit_Display hex_digit_display_2 (.value({in_10, in_9, in_8, in_7}));  // open: dp
  Hex_Digit_Display hex_digit_display_3 (.value({in_15, in_14, in_13, in_11}));  // open: dp
  Hex_Digit_Display hex_digit_display_4 (.value({in_20, in_19, in_18, in_17}));  // open: dp
  Hex_Digit_Display hex_digit_display_5 (.value({undriven, out_22, out_21}));  // open: dp
  // Pins of 2 and 4 bits meet at {undriven, out_22, out_21}
endmodule
