// Logisim project q1.circ as structural Verilog: 2 circuits, main circuit full adder using 4x1 Mux
module full_adder_using_4x1_Mux (
  input  a,
  input  [1:0] b_and_c,
  output sum,
  output carry
);

  wire not_1_out;

  not not_1 (not_1_out, a);
  Multiplexer #(.select(2), .enable("false")) multiplexer_1 (
    .in0(a), .in1(not_1_out), .in2(not_1_out), .in3(a), .out(sum), .sel(b_and_c));
  Multiplexer #(.select(2), .enable("false")) multiplexer_2 (
    .in0(1'b0), .in1(a), .in2(a), .in3(1'b1), .out(carry), .sel(b_and_c));

  // Notes on the sheet:
  //   221b307
endmodule

module full_adder_using_8x1_Mux (
  input  [2:0] a_and_b_and_c,
  output carry,
  output sum
);

  Multiplexer #(.select(3), .enable("false")) multiplexer_1 (
    .in0(1'b0), .in1(1'b0), .in2(1'b0), .in3(1'b1), .in4(1'b0), .in5(1'b1), .in6(1'b1), .in7(1'b1),
    .out(carry), .sel(a_and_b_and_c));
  Multiplexer #(.select(3), .enable("false")) multiplexer_2 (
    .in0(1'b0), .in1(1'b1), .in2(1'b1), .in3(1'b0), .in4(1'b1), .in5(1'b0), .in6(1'b0), .in7(1'b1),
    .out(sum), .sel(a_and_b_and_c));

  // Notes on the sheet:
  //   221b307
endmodule
