// Logisim project q2.circ as structural Verilog: 1 circuit, main circuit main
module main (
  input  a,
  input  b,
  input  c,
  output even,
  output odd,
  output prime
);

  wire and_1_out, and_2_out, not_1_out;

  Hex_Digit_Display hex_digit_display_1 (.value({1'b0, a, b, c}));  // open: dp
  not not_1 (not_1_out, a);
  and and_1 (and_1_out, not_1_out, b);
  _7_Segment_Display u_7_segment_display_1 (.g(even), .f(even), .a(even), .e(even), .d(even));  // open: b, c, dp
  and and_2 (and_2_out, a, c);
  _7_Segment_Display u_7_segment_display_2 (.f(c), .a(c), .b(c), .e(c), .d(c), .c(c));  // open: g, dp
  not not_2 (even, c);
  or or_1 (prime, and_2_out, and_1_out);
  _7_Segment_Display u_7_segment_display_3 (.g(prime), .f(prime), .a(prime), .b(prime), .e(prime));  // open: d, c, dp

  assign odd = c;

  // Notes on the sheet:
  //   221b307
endmodule
