// Logisim project q3.circ as structural Verilog: 1 circuit, main circuit main
module main (
  input  Leap_Year_bit,
  input  m0,
  input  m1,
  input  m2,
  input  m3,
  output _28,
  output _29,
  output _30,
  output _31
);

  wire and_3_out, and_4_out, and_5_out, and_6_out, and_7_out, not_1_out, not_2_out, not_3_out, not_4_out,
       not_5_out;

  not not_1 (not_1_out, m0);
  not not_2 (not_2_out, m1);
  not not_3 (not_3_out, m2);
  not not_4 (not_4_out, m3);
  Hex_Digit_Display hex_digit_display_1 (.value({m3, m2, m1, m0}));  // open: dp
  not not_5 (not_5_out, Leap_Year_bit);
  Hex_Digit_Display hex_digit_display_2 (.value({3'b000, Leap_Year_bit}));  // open: dp
  and and_1 (_28, not_4_out, not_3_out, not_5_out, m1, not_1_out);
  and and_2 (_29, Leap_Year_bit, not_4_out, not_3_out, m1, not_1_out);
  and and_3 (and_3_out, m3, not_3_out, m0);
  or or_1 (_30, and_3_out, and_4_out);
  and and_4 (and_4_out, not_4_out, m2, not_1_out);
  and and_5 (and_5_out, not_4_out, m0);
  or or_2 (_31, and_5_out, and_6_out, and_7_out);
  and and_6 (and_6_out, m3, not_2_out, not_1_out);
  and and_7 (and_7_out, m3, not_3_out, not_1_out);
  _7_Segment_Display u_7_segment_display_1 (.g(_28), .a(_28), .b(_28), .e(_28), .d(_28));  // open: f, c, dp
  _7_Segment_Display u_7_segment_display_2 (.g(_29), .a(_29), .b(_29), .e(_29), .d(_29));  // open: f, c, dp
  _7_Segment_Display u_7_segment_display_3 (.g(_30), .a(_30), .b(_30), .d(_30), .c(_30));  // open: f, e, dp
  _7_Segment_Display u_7_segment_display_4 (.g(_31), .a(_31), .b(_31), .d(_31), .c(_31));  // open: f, e, dp
  _7_Segment_Display u_7_segment_display_5 (.g(_28), .f(_28), .a(_28), .b(_28), .e(_28), .d(_28), .c(_28));  // open: dp
  _7_Segment_Display u_7_segment_display_6 (.g(_29), .f(_29), .a(_29), .b(_29), .d(_29), .c(_29));  // open: e, dp
  _7_Segment_Display u_7_segment_display_7 (.f(_30), .a(_30), .b(_30), .e(_30), .d(_30), .c(_30));  // open: g, dp
  _7_Segment_Display u_7_segment_display_8 (.b(_31), .c(_31));  // open: g, f, a, e, d, dp

  // Notes on the sheet:
  //   Month
  //   Leap year
  //   221b307
endmodule
