// Logisim project q4.circ as structural Verilog: 1 circuit, main circuit main
module main (
  input  o3,
  input  o2,
  input  o1,
  input  o0,
  input  t3,
  input  t2,
  input  t1,
  input  t0,
  input  h3,
  input  h2,
  input  h1,
  input  h0,
  input  th3,
  input  th2,
  input  th1,
  input  th0,
  output out_17
);

  wire and_1_out, and_2_out, and_3_out, and_4_out, and_5_out, not_1_out, not_2_out, not_3_out, not_4_out,
       not_5_out, not_6_out, not_7_out, not_8_out, not_9_out, or_1_out;

  not not_1 (not_1_out, o3);
  not not_2 (not_2_out, o2);
  not not_3 (not_3_out, o1);
  not not_4 (not_4_out, o0);
  not not_5 (not_5_out, t3);
  not not_6 (not_6_out, t2);
  not not_7 (not_7_out, t1);
  not not_8 (not_8_out, t0);
  Hex_Digit_Display hex_digit_display_1 (.value({th3, th2, th1, th0}));  // open: dp
  and and_1 (and_1_out, not_8_out, not_4_out, not_3_out);
  and and_2 (and_2_out, t0, o1, not_4_out);
  Hex_Digit_Display hex_digit_display_2 (.value({h3, h2, h1, h0}));  // open: dp
  or or_1 (or_1_out, and_1_out, and_2_out);
  and and_3 (and_3_out, not_1_out, not_2_out, not_3_out, not_4_out, not_5_out, not_6_out, not_7_out, not_8_out);
  Hex_Digit_Display hex_digit_display_3 (.value({t3, t2, t1, t0}));  // open: dp
  and and_4 (and_4_out, or_1_out, not_9_out);
  not not_9 (not_9_out, and_3_out);
  or or_2 (out_17, and_4_out, and_5_out);
  and and_5 (and_5_out, or_1_out, and_3_out);
  Hex_Digit_Display hex_digit_display_4 (.value({o3, o2, o1, o0}));  // open: dp
  Hex_Digit_Display hex_digit_display_5 (.value({3'b000, out_17}));  // open: dp

  // Notes on the sheet:
  //   221b307
  //   D100
  //   Year
  //   D4
  //   D400
  //   Leap year 
endmodule
