// Logisim project activity 4 (221b312).circ as structural Verilog: 1 circuit, main circuit main
// B3
module main (
  input  in_1,
  input  in_2,
  input  A0,
  input  A1,
  input  A2,
  input  A3,
  input  [3:0] in_7,
  input  B0,
  input  B1,
  input  B2,
  input  B3,
  input  in_12
);

  Multiplexer #(.select(2)) multiplexer_1 (
    .in0(B2), .in1(A2), .in2(A0), .in3(B2), .out(in_7[0]), .en(in_1));  // open: sel
  Multiplexer #(.select(2)) multiplexer_2 (
    .in0(B1), .in1(A2), .in2(A2), .in3(B2), .out(in_7[1]), .en(in_1));  // open: sel
  Multiplexer #(.select(2)) multiplexer_3 (
    .in0(B0), .in1(A2), .in2(A2), .in3(B0), .out(in_7[2]), .en(in_1));  // open: sel
  Multiplexer #(.select(2)) multiplexer_4 (
    .in0(in_12), .in1(A1), .in2(A1), .in3(B3), .out(in_7[3]), .en(in_1));  // open: sel

  assign A3 = A2;
  assign in_2 = in_1;
endmodule
