// Logisim project q1.circ as structural Verilog: 1 circuit, main circuit main
module main (
  input  a0,
  input  a1,
  input  a2,
  input  a3,
  input  b0,
  input  b1,
  input  b2,
  input  b3,
  input  c0,
  input  c1,
  input  c2,
  input  c3,
  input  d0,
  input  d1,
  input  [1:0] in_15,
  input  d2,
  input  d3,
  output x0,
  output x1,
  output x2,
  output x3
);

  Multiplexer #(.select(2), .enable("false")) multiplexer_1 (
    .in0(a0), .in1(b0), .in2(c0), .in3(d0), .out(x0), .sel(in_15));
  Multiplexer #(.select(2), .enable("false")) multiplexer_2 (
    .in0(a1), .in1(b1), .in2(c1), .in3(d1), .out(x1), .sel(in_15));
  Multiplexer #(.select(2), .enable("false")) multiplexer_3 (
    .in0(a2), .in1(b2), .in2(c2), .in3(d2), .out(x2), .sel(in_15));
  Multiplexer #(.select(2), .enable("false")) multiplexer_4 (
    .in0(a3), .in1(b3), .in2(c3), .in3(d3), .out(x3), .sel(in_15));
endmodule
