// Logisim project q2.circ as structural Verilog: 1 circuit, main circuit main
module main (
  input  a0,
  input  a1,
  input  a2,
  input  a3,
  input  b0,
  input  b1,
  input  b2,
  input  b3,
  input  c0,
  input  c1,
  input  c2,
  input  c3,
  input  d0,
  input  d1,
  input  d2,
  input  d3,
  input  [1:0] select,
  output x0,
  output x1,
  output x2,
  output x3
);

  wire decoder_1_out0, decoder_1_out1, decoder_1_out2, decoder_1_out3;

  assign x2 = decoder_1_out0 ? a2 : 1'bz;  // Controlled_Buffer controlled_buffer_1
  assign x3 = decoder_1_out0 ? a3 : 1'bz;  // Controlled_Buffer controlled_buffer_2
  assign x0 = decoder_1_out1 ? b0 : 1'bz;  // Controlled_Buffer controlled_buffer_3
  assign x1 = decoder_1_out1 ? b1 : 1'bz;  // Controlled_Buffer controlled_buffer_4
  assign x0 = decoder_1_out2 ? c0 : 1'bz;  // Controlled_Buffer controlled_buffer_5
  assign x0 = decoder_1_out3 ? d0 : 1'bz;  // Controlled_Buffer controlled_buffer_6
  assign x1 = decoder_1_out3 ? d1 : 1'bz;  // Controlled_Buffer controlled_buffer_7
  assign x0 = decoder_1_out0 ? a0 : 1'bz;  // Controlled_Buffer controlled_buffer_8
  assign x1 = decoder_1_out0 ? a1 : 1'bz;  // Controlled_Buffer controlled_buffer_9
  assign x2 = decoder_1_out1 ? b2 : 1'bz;  // Controlled_Buffer controlled_buffer_10
  assign x3 = decoder_1_out1 ? b3 : 1'bz;  // Controlled_Buffer controlled_buffer_11
  assign x1 = decoder_1_out2 ? c1 : 1'bz;  // Controlled_Buffer controlled_buffer_12
  assign x2 = decoder_1_out2 ? c2 : 1'bz;  // Controlled_Buffer controlled_buffer_13
  assign x2 = decoder_1_out3 ? d2 : 1'bz;  // Controlled_Buffer controlled_buffer_14
  assign x3 = decoder_1_out3 ? d3 : 1'bz;  // Controlled_Buffer controlled_buffer_15
  assign x3 = decoder_1_out2 ? c3 : 1'bz;  // Controlled_Buffer controlled_buffer_16
  Decoder #(.select(2), .enable("false")) decoder_1 (
    .out0(decoder_1_out0), .out1(decoder_1_out1), .out2(decoder_1_out2), .out3(decoder_1_out3), .sel(select));
endmodule
