// Logisim project q3.circ as structural Verilog: 1 circuit, main circuit main
module main (
  input  [3:0] a,
  input  [3:0] b,
  input  s1,
  input  s0,
  output [3:0] f
);

  wire [3:0] and_1_out, not_1_out, or_1_out, xor_1_out;

  assign not_1_out = ~a;  // NOT_Gate not_1, 4 bits wide
  assign and_1_out = a & b;  // AND_Gate and_1, 4 bits wide
  assign or_1_out = a | b;  // OR_Gate or_1, 4 bits wide
  assign xor_1_out = a ^ b;  // XOR_Gate xor_1, 4 bits wide
  Multiplexer #(.select(2), .width(4), .enable("false")) multiplexer_1 (
    .in0(not_1_out), .in1(and_1_out), .in2(or_1_out), .in3(xor_1_out), .out(f), .sel({s1, s0}));
endmodule
