// Logisim project q4.circ as structural Verilog: 1 circuit, main circuit main
module main (
  input  a0,
  input  a1,
  input  a2,
  input  a3,
  input  b0,
  input  b1,
  input  b2,
  input  b3,
  input  [1:0] select,
  output f0,
  output f1,
  output f2,
  output f3
);

  Multiplexer #(.select(2), .enable("false")) multiplexer_1 (
    .in0(1'b0), .in1(b1), .in2(a1), .in3(b3), .out(f0), .sel(select));
  Multiplexer #(.select(2), .enable("false")) multiplexer_2 (
    .in0(a0), .in1(b2), .in2(a2), .in3(b0), .out(f1), .sel(select));
  Multiplexer #(.select(2), .enable("false")) multiplexer_3 (
    .in0(a1), .in1(b3), .in2(1'b0), .in3(b1), .out(f2), .sel(select));
  Multiplexer #(.select(2), .enable("false")) multiplexer_4 (
    .in0(a2), .in1(b0), .in2(a3), .in3(b2), .out(f3), .sel(select));
endmodule
