// Logisim project 2 (221b312).circ as structural Verilog: 1 circuit, main circuit main
module main (
  input  [3:0] in_1,
  input  [3:0] in_2,
  input  [3:0] in_3,
  input  [3:0] in_4,
  input  [3:0] in_5,
  input  s0,
  input  s1
);

  Hex_Digit_Display hex_digit_display_1 (.value(in_1));  // open: dp
  Hex_Digit_Display hex_digit_display_2 (.value(in_2));  // open: dp
  Hex_Digit_Display hex_digit_display_3 (.value(in_4));  // open: dp
  Hex_Digit_Display hex_digit_display_4 (.value(in_5));  // open: dp
  Multiplexer #(.select(2)) multiplexer_1 (
    .in0(in_1[0]), .in1(in_2[0]), .in2(in_4[0]), .in3(in_5[0]), .out(in_3[0]), .en(s0));  // open: sel
  Multiplexer #(.select(2)) multiplexer_2 (
    .in0(in_1[1]), .in1(in_2[1]), .in2(in_4[1]), .in3(in_5[1]), .out(in_3[1]), .en(s0));  // open: sel
  Multiplexer #(.select(2)) multiplexer_3 (
    .in0(in_1[2]), .in1(in_2[2]), .in2(in_4[2]), .in3(in_5[2]), .out(in_3[2]), .en(s0));  // open: sel
  Multiplexer #(.select(2)) multiplexer_4 (
    .in0(in_1[3]), .in1(in_2[3]), .in2(in_4[3]), .in3(in_5[3]), .out(in_3[3]), .en(s0));  // open: sel
  Hex_Digit_Display hex_digit_display_5 (.value(in_3));  // open: dp

  assign s1 = s0;
endmodule
