// Logisim project activity 1 (221b312).circ as structural Verilog: 1 circuit, main circuit main
module main (
  input  in_1,
  input  in_2,
  input  in_3,
  input  in_4,
  input  in_5,
  input  [3:0] in_6,
  input  in_7,
  input  in_8,
  input  in_9,
  input  in_10,
  input  in_11,
  input  in_12,
  input  in_13,
  input  in_14,
  input  in_15,
  input  in_16,
  input  in_17,
  input  in_18,
  input  in_19
);

  Multiplexer #(.select(2)) multiplexer_1 (
    .in0(in_1), .in1(in_5), .in2(in_10), .in3(in_14), .out(in_6[0]), .en(in_18));  // open: sel
  Multiplexer #(.select(2)) multiplexer_2 (
    .in0(in_2), .in1(in_7), .in2(in_11), .in3(in_15), .out(in_6[1]), .en(in_18));  // open: sel
  Multiplexer #(.select(2)) multiplexer_3 (
    .in0(in_8), .in1(in_12), .in3(in_16), .out(in_6[2]), .en(in_18));  // open: in2, sel
  Multiplexer #(.select(2)) multiplexer_4 (
    .in0(in_4), .in1(in_9), .in2(in_13), .in3(in_17), .out(in_6[3]), .en(in_18));  // open: sel

  assign in_19 = in_18;
endmodule
