// Logisim project activity 2 (221b312).circ as structural Verilog: 1 circuit, main circuit main
module main (
  input  in_1,
  input  in_2,
  input  in_3,
  input  in_4,
  input  in_5,
  input  in_6,
  input  in_7,
  input  in_8,
  input  [1:0] in_9,
  input  in_10,
  input  in_11,
  input  in_12,
  input  in_13,
  input  in_14,
  input  in_15,
  input  in_16,
  input  in_17,
  output out_18,
  output out_19,
  output out_20,
  output out_21
);

  wire decoder_1_out0, decoder_1_out1, decoder_1_out2, decoder_1_out3;

  assign out_18 = decoder_1_out0 ? in_1 : 1'bz;  // Controlled_Buffer controlled_buffer_1
  assign out_18 = decoder_1_out0 ? in_2 : 1'bz;  // Controlled_Buffer controlled_buffer_2
  assign out_18 = decoder_1_out0 ? in_3 : 1'bz;  // Controlled_Buffer controlled_buffer_3
  assign out_18 = decoder_1_out0 ? in_4 : 1'bz;  // Controlled_Buffer controlled_buffer_4
  assign out_19 = decoder_1_out1 ? in_5 : 1'bz;  // Controlled_Buffer controlled_buffer_5
  assign out_19 = decoder_1_out1 ? in_6 : 1'bz;  // Controlled_Buffer controlled_buffer_6
  assign out_19 = decoder_1_out1 ? in_7 : 1'bz;  // Controlled_Buffer controlled_buffer_7
  assign out_19 = decoder_1_out1 ? in_8 : 1'bz;  // Controlled_Buffer controlled_buffer_8
  assign out_20 = decoder_1_out2 ? in_10 : 1'bz;  // Controlled_Buffer controlled_buffer_9
  assign out_20 = decoder_1_out2 ? in_11 : 1'bz;  // Controlled_Buffer controlled_buffer_10
  assign out_20 = decoder_1_out2 ? in_12 : 1'bz;  // Controlled_Buffer controlled_buffer_11
  assign out_20 = decoder_1_out2 ? in_13 : 1'bz;  // Controlled_Buffer controlled_buffer_12
  assign out_21 = decoder_1_out3 ? in_14 : 1'bz;  // Controlled_Buffer controlled_buffer_13
  assign out_21 = decoder_1_out3 ? in_15 : 1'bz;  // Controlled_Buffer controlled_buffer_14
  assign out_21 = decoder_1_out3 ? in_16 : 1'bz;  // Controlled_Buffer controlled_buffer_15
  assign out_21 = decoder_1_out3 ? in_17 : 1'bz;  // Controlled_Buffer controlled_buffer_16
  Decoder #(.select(2)) decoder_1 (
    .out0(decoder_1_out0), .out1(decoder_1_out1), .out2(decoder_1_out2), .out3(decoder_1_out3), .sel(in_9));  // open: en
endmodule
