// Logisim project activity 3 (221b312).circ as structural Verilog: 1 circuit, main circuit main
module main (
  input  in_1,
  input  in_2,
  input  [3:0] in_3,
  input  in_4,
  input  in_5,
  input  in_6,
  input  in_7,
  input  in_8,
  input  in_9,
  input  in_10,
  input  in_11
);

  wire and_1_out, and_2_out, and_3_out, and_4_out, not_1_out, not_2_out, not_3_out, not_4_out, or_1_out,
       or_2_out, or_3_out, or_4_out, xor_1_out, xor_2_out, xor_3_out, xor_4_out;

  xor xor_1 (xor_1_out, in_1, in_2);
  or or_1 (or_1_out, in_1, in_2);
  or or_2 (or_2_out, in_4, in_5);
  xor xor_2 (xor_2_out, in_4, in_5);
  xor xor_3 (xor_3_out, in_6, in_7);
  xor xor_4 (xor_4_out, in_8, in_9);
  and and_1 (and_1_out, in_1, in_2);
  and and_2 (and_2_out, in_4, in_5);
  and and_3 (and_3_out, in_6, in_7);
  or or_3 (or_3_out, in_6, in_7);
  and and_4 (and_4_out, in_8, in_9);
  or or_4 (or_4_out, in_8, in_9);
  not not_1 (not_1_out, in_1);
  Multiplexer #(.select(2)) multiplexer_1 (
    .in0(not_1_out), .in1(and_1_out), .in2(or_1_out), .in3(xor_1_out), .out(in_3[0]), .en(in_10));  // open: sel
  not not_2 (not_2_out, in_4);
  Multiplexer #(.select(2)) multiplexer_2 (
    .in0(not_2_out), .in1(and_2_out), .in2(or_2_out), .in3(xor_2_out), .out(in_3[1]), .en(in_10));  // open: sel
  not not_3 (not_3_out, in_6);
  not not_4 (not_4_out, in_8);
  Multiplexer #(.select(2)) multiplexer_3 (
    .in0(not_3_out), .in1(and_3_out), .in2(or_3_out), .in3(xor_3_out), .out(in_3[2]), .en(in_10));  // open: sel
  Multiplexer #(.select(2)) multiplexer_4 (
    .in0(not_4_out), .in1(and_4_out), .in2(or_4_out), .in3(xor_4_out), .out(in_3[3]), .en(in_10));  // open: sel

  assign in_11 = in_10;
endmodule
