// Logisim project q1.circ as structural Verilog: 1 circuit, main circuit main
module main (
  input  s2,
  input  s1,
  input  Cin,
  input  a3,
  input  a2,
  input  a1,
  input  a0,
  input  b3,
  input  b2,
  input  b1,
  input  b0
);

  wire [0:0] adder_1_cout;
  wire [2:2] not_1_out;
  wire [3:0] adder_1_out, and_1_out, and_2_out, multiplexer_1_out, multiplexer_2_out, multiplexer_3_out,
       multiplexer_4_out, multiplexer_5_out, not_2_out, shifter_1_out, shifter_2_out, xor_1_out;

  assign and_1_out = not_2_out & 4'b0001;  // AND_Gate and_1, 4 bits wide
  not not_1 (not_1_out[2], 1'b1);
  assign not_2_out = ~{b3, b2, b1, b0};  // NOT_Gate not_2, 4 bits wide
  Multiplexer #(.select(2), .width(4), .enable("false")) multiplexer_1 (
    .in0(4'b0000), .in1(and_1_out), .in2({b3, b2, b1, b0}), .in3({1'b1, not_1_out[2], 2'b11}),
    .out(multiplexer_1_out), .sel({s1, Cin}));
  Hex_Digit_Display hex_digit_display_1 (.value({a3, a2, a1, a0}));  // open: dp
  Adder #(.width(4)) adder_1 (
    .a({a3, a2, a1, a0}), .b(multiplexer_1_out), .out(adder_1_out), .cin(Cin), .cout(adder_1_cout[0]));
  assign xor_1_out = {a3, a2, a1, a0} ^ {b3, b2, b1, b0};  // XOR_Gate xor_1, 4 bits wide
  assign and_2_out = {a3, a2, a1, a0} & {b3, b2, b1, b0};  // AND_Gate and_2, 4 bits wide
  Hex_Digit_Display hex_digit_display_2 (.value({b3, b2, b1, b0}));  // open: dp
  Multiplexer #(.width(4), .enable("false")) multiplexer_2 (
    .in0(xor_1_out), .in1(and_2_out), .out(multiplexer_2_out), .sel(Cin));
  Shifter #(.width(4), .shift("rl")) shifter_1 (.in({a3, a2, a1, a0}), .\dist (2'b01), .out(shifter_1_out));
  Multiplexer #(.width(4), .enable("false")) multiplexer_3 (
    .in0(shifter_1_out), .in1(shifter_2_out), .out(multiplexer_3_out), .sel(Cin));
  Shifter #(.width(4), .shift("ar")) shifter_2 (.in({a3, a2, a1, a0}), .\dist (2'b01), .out(shifter_2_out));
  Multiplexer #(.width(4), .enable("false")) multiplexer_4 (
    .in0(multiplexer_2_out), .in1(multiplexer_3_out), .out(multiplexer_4_out), .sel(s1));
  Multiplexer #(.width(4), .enable("false")) multiplexer_5 (
    .in0(adder_1_out), .in1(multiplexer_4_out), .out(multiplexer_5_out), .sel(s2));
  Hex_Digit_Display hex_digit_display_3 (.value(multiplexer_5_out));  // open: dp
  Hex_Digit_Display hex_digit_display_4 (.value({3'b000, adder_1_cout[0]}));  // open: dp

  // Notes on the sheet:
  //   a
  //   b
  //   output
  //   Cout
endmodule
