// Logisim project q2.circ as structural Verilog: 2 circuits, main circuit main
module main (
  input  a1,
  input  a0,
  input  b1,
  input  b0,
  output o0,
  output o1,
  output o2,
  output o3
);

  wire half_adder_1_cout, half_adder_1_output, half_adder_2_cout, half_adder_2_output, half_adder_3_output,
       half_adder_4_cout, half_adder_4_output, half_adder_5_cout, half_adder_5_output, half_adder_6_output,
       half_adder_7_cout, half_adder_7_output;

  half_adder half_adder_1 (.a(a0), .b(a0), .Cout(half_adder_1_cout), .\output (half_adder_1_output));
  half_adder half_adder_2 (.a(a1), .b(a1), .Cout(half_adder_2_cout), .\output (half_adder_2_output));
  Hex_Digit_Display hex_digit_display_1 (.value({2'b00, a1, a0}));  // open: dp
  half_adder half_adder_3 (
    .a(half_adder_1_cout), .b(half_adder_2_output), .\output (half_adder_3_output));  // open: Cout
  half_adder half_adder_4 (.a(half_adder_3_output), .b(a1), .Cout(half_adder_4_cout), .\output (half_adder_4_output));
  Hex_Digit_Display hex_digit_display_2 (.value({2'b00, b1, b0}));  // open: dp
  half_adder half_adder_5 (.a(half_adder_1_output), .b(a0), .Cout(half_adder_5_cout), .\output (half_adder_5_output));
  half_adder half_adder_6 (
    .a(half_adder_5_cout), .b(half_adder_4_output), .\output (half_adder_6_output));  // open: Cout
  half_adder half_adder_7 (
    .a(half_adder_4_cout), .b(half_adder_2_cout), .Cout(half_adder_7_cout), .\output (half_adder_7_output));
  Multiplexer #(.select(2), .enable("false")) multiplexer_1 (
    .in0(1'b0), .in1(a0), .in2(half_adder_1_output), .in3(half_adder_5_output), .out(o0), .sel({b1, b0}));
  Multiplexer #(.select(2), .enable("false")) multiplexer_2 (
    .in0(1'b0), .in1(a1), .in2(half_adder_3_output), .in3(half_adder_6_output), .out(o1), .sel({b1, b0}));
  Multiplexer #(.select(2), .enable("false")) multiplexer_3 (
    .in0(1'b0), .in1(1'b0), .in2(half_adder_2_cout), .in3(half_adder_7_output), .out(o2), .sel({b1, b0}));
  Multiplexer #(.select(2), .enable("false")) multiplexer_4 (
    .in0(1'b0), .in1(1'b0), .in2(1'b0), .in3(half_adder_7_cout), .out(o3), .sel({b1, b0}));
  Hex_Digit_Display hex_digit_display_3 (.value({o3, o2, o1, o0}));  // open: dp

  // Notes on the sheet:
  //   X
endmodule

module half_adder (
  input  a,
  input  b,
  output \output ,
  output Cout
);

  xor xor_1 (\output , a, b);
  and and_1 (Cout, a, b);
endmodule
