// Logisim project activity 2.circ as structural Verilog: 2 circuits, main circuit main
module main (
  input  in_1,
  output out_2
);

  wire clock_1_out, nand_1_out, nand_2_out, nand_4_out, not_1_out;

  not not_1 (not_1_out, in_1);
  Clock clock_1 (.out(clock_1_out));
  not nand_1 (nand_1_out, in_1);  // NAND_Gate
  nand nand_2 (nand_2_out, not_1_out, clock_1_out);
  nand nand_3 (out_2, nand_1_out, nand_4_out);
  nand nand_4 (nand_4_out, out_2, nand_2_out);
endmodule

module d_flip_flop (
  input  in_1,
  input  in_2,
  output out_3
);

  wire clock_1_out, main_1_p4, main_2_p4, main_3_p4;

  Clock clock_1 (.out(clock_1_out));
  // main main_1: pin names not known; wires that end beside it: in_1, clock_1_out, in_2, main_1_p4
  // main main_2: pin names not known; wires that end beside it: main_1_p4, clock_1_out, in_2, main_2_p4
  // main main_3: pin names not known; wires that end beside it: main_2_p4, clock_1_out, in_2, main_3_p4
  main main_4 (.in_1(clock_1_out), .out_2(out_3));
endmodule
