// Logisim project q2.circ as structural Verilog: 3 circuits, main circuit main
module main (
  input  clear,
  input  enable,
  output Q0
);

  wire clock_out, d_ff_1_q, d_ff_2_q, d_ff_3_q, Serial_Data_in_out;

  Clock Serial_Data_in (.out(Serial_Data_in_out));
  D_Flip_Flop d_ff_1 (
    .clk(clock_out), .D(Serial_Data_in_out), .Q(d_ff_1_q), .en(enable), .reset(clear));  // open: Qn, preset
  Clock clock (.out(clock_out));
  D_flip_flop d_flip_flop_1 ();  // open: clock, D, Clear, Q, Qnot
  D_Flip_Flop d_ff_2 (.clk(clock_out), .D(d_ff_1_q), .Q(d_ff_2_q), .en(enable), .reset(clear));  // open: Qn, preset
  D_Flip_Flop d_ff_3 (.clk(clock_out), .D(d_ff_2_q), .Q(d_ff_3_q), .en(enable), .reset(clear));  // open: Qn, preset
  D_Flip_Flop d_ff_4 (.clk(clock_out), .D(d_ff_3_q), .Q(Q0), .en(enable), .reset(clear));  // open: Qn, preset
endmodule

module D_flip_flop (
  input  clock,
  input  D,
  input  Clear,
  output Q,
  output Qnot
);

  wire nand_1_out, nand_2_out, nand_3_out, nand_4_out, nand_5_out, nand_6_out, not_1_out, not_2_out,
       not_3_out, not_4_out;

  not not_1 (not_1_out, 1'b0);
  not not_2 (not_2_out, D);
  nand nand_1 (nand_1_out, D, 1'b1, clock);
  nand nand_2 (nand_2_out, clock, 1'b1, not_2_out);
  not not_3 (not_3_out, clock);
  nand nand_3 (nand_3_out, not_1_out, nand_1_out, nand_4_out);
  nand nand_4 (nand_4_out, nand_3_out, nand_2_out, not_4_out);
  nand nand_5 (nand_5_out, nand_3_out, not_3_out);
  nand nand_6 (nand_6_out, nand_4_out, not_3_out);
  not not_4 (not_4_out, Clear);
  nand nand_7 (Q, not_1_out, nand_5_out, Qnot);
  nand nand_8 (Qnot, Q, nand_6_out, not_4_out);

  // Notes on the sheet:
  //   221b307
endmodule

module using_inbuilt (
  input  Serial_data_in,
  input  clear,
  output out_3
);

  wire clock_1_out, d_flip_flop_1_q, d_flip_flop_2_q, d_flip_flop_3_q;

  Clock clock_1 (.out(clock_1_out));
  D_flip_flop d_flip_flop_1 (
    .clock(clock_1_out), .D(Serial_data_in), .Clear(clear), .Q(d_flip_flop_1_q));  // open: Qnot
  D_flip_flop d_flip_flop_2 (
    .clock(clock_1_out), .D(d_flip_flop_1_q), .Clear(clear), .Q(d_flip_flop_2_q));  // open: Qnot
  D_flip_flop d_flip_flop_3 (
    .clock(clock_1_out), .D(d_flip_flop_2_q), .Clear(clear), .Q(d_flip_flop_3_q));  // open: Qnot
  D_flip_flop d_flip_flop_4 (.clock(clock_1_out), .D(d_flip_flop_3_q), .Clear(clear), .Q(out_3));  // open: Qnot

  // Notes on the sheet:
  //   221b307
endmodule
