// Logisim project q3.circ as structural Verilog: 1 circuit, main circuit main
module main (
  input  reset,
  output Qa,
  output Qb,
  output Qc
);

  wire and_1_out, clock_1_out, d_ff_1_qn, d_ff_2_qn, d_ff_3_qn, or_1_out;

  Clock clock_1 (.out(clock_1_out));
  D_Flip_Flop d_ff_1 (.clk(clock_1_out), .D(d_ff_1_qn), .Q(Qa), .Qn(d_ff_1_qn), .reset(or_1_out));  // open: preset, en
  Hex_Digit_Display hex_digit_display_1 (.value({1'b0, Qc, Qb, Qa}));  // open: dp
  D_Flip_Flop d_ff_2 (.clk(d_ff_1_qn), .D(d_ff_2_qn), .Q(Qb), .Qn(d_ff_2_qn), .reset(or_1_out));  // open: preset, en
  or or_1 (or_1_out, and_1_out, reset);
  D_Flip_Flop d_ff_3 (.clk(d_ff_2_qn), .D(d_ff_3_qn), .Q(Qc), .Qn(d_ff_3_qn), .reset(or_1_out));  // open: preset, en
  and and_1 (and_1_out, Qc, Qb);
endmodule
