// Logisim project q4.circ as structural Verilog: 4 circuits, main circuit main
module main (
  input  reset
);

  wire and_1_out, clock_1_out, or_1_out, undriven;
  wire [3:0] mod_3_1_o0, mod_6_1_o0, mod_6_2_o0, mod_10_1_o0, mod_10_2_o0, mod_10_3_o0;

  Clock clock_1 (.out(clock_1_out));
  Hex_Digit_Display hex_digit_display_1 (.value(mod_3_1_o0));  // open: dp
  mod_3 mod_3_1 (
    .reset(or_1_out), .o0(mod_3_1_o0[0]), .o1(mod_3_1_o0[1]), .o2(mod_3_1_o0[2]), .o3(mod_3_1_o0[3]));  // open: clock
  Hex_Digit_Display hex_digit_display_2 (.value(mod_10_1_o0));  // open: dp
  mod_10 mod_10_1 (
    .reset(or_1_out), .o0(mod_10_1_o0[0]), .o1(mod_10_1_o0[1]), .o2(mod_10_1_o0[2]), .o3(mod_10_1_o0[3]));  // open: clock
  and and_1 (and_1_out, mod_10_1_o0[1], mod_3_1_o0[2]);
  or or_1 (or_1_out, and_1_out, reset);
  Hex_Digit_Display hex_digit_display_3 (.value(mod_6_1_o0));  // open: dp
  mod_6 mod_6_1 (
    .reset(or_1_out), .o0(mod_6_1_o0[0]), .o1(mod_6_1_o0[1]), .o2(mod_6_1_o0[2]), .o3(mod_6_1_o0[3]));  // open: clock
  Hex_Digit_Display hex_digit_display_4 (.value(mod_10_2_o0));  // open: dp
  mod_10 mod_10_2 (
    .reset(or_1_out), .o0(mod_10_2_o0[0]), .o1(mod_10_2_o0[1]), .o2(mod_10_2_o0[2]), .o3(mod_10_2_o0[3]));  // open: clock
  mod_6 mod_6_2 (
    .clock(undriven), .reset(or_1_out), .o0(mod_6_2_o0[0]), .o1(mod_6_2_o0[1]), .o2(mod_6_2_o0[2]),
    .o3(mod_6_2_o0[3]));
  Hex_Digit_Display hex_digit_display_5 (.value(mod_6_2_o0));  // open: dp
  Hex_Digit_Display hex_digit_display_6 (.value(mod_10_3_o0));  // open: dp
  mod_10 mod_10_3 (
    .clock(clock_1_out), .reset(or_1_out), .o0(mod_10_3_o0[0]), .o1(mod_10_3_o0[1]), .o2(mod_10_3_o0[2]),
    .o3(mod_10_3_o0[3]));
endmodule

module mod_3 (
  input  clock,
  input  reset,
  output o0,
  output o1,
  output o2,
  output o3
);

  wire and_1_out, d_ff_1_qn, d_ff_2_qn, d_ff_3_qn, or_1_out;

  D_Flip_Flop d_ff_1 (.clk(clock), .D(d_ff_1_qn), .Q(o0), .Qn(d_ff_1_qn), .reset(or_1_out));  // open: preset, en
  D_Flip_Flop d_ff_2 (.clk(d_ff_1_qn), .D(d_ff_2_qn), .Q(o1), .Qn(d_ff_2_qn), .reset(or_1_out));  // open: preset, en
  or or_1 (or_1_out, and_1_out, reset);
  D_Flip_Flop d_ff_3 (.clk(d_ff_2_qn), .D(d_ff_3_qn), .Q(o2), .Qn(d_ff_3_qn), .reset(or_1_out));  // open: preset, en
  and and_1 (and_1_out, o0, o1);

  assign o3 = 1'b0;

  // Notes on the sheet:
  //   221b307
endmodule

module mod_6 (
  input  clock,
  input  reset,
  output o0,
  output o1,
  output o2,
  output o3
);

  wire and_1_out, d_ff_1_qn, d_ff_2_qn, d_ff_3_qn, or_1_out;

  D_Flip_Flop d_ff_1 (.clk(clock), .D(d_ff_1_qn), .Q(o0), .Qn(d_ff_1_qn), .reset(or_1_out));  // open: preset, en
  D_Flip_Flop d_ff_2 (.clk(d_ff_1_qn), .D(d_ff_2_qn), .Q(o1), .Qn(d_ff_2_qn), .reset(or_1_out));  // open: preset, en
  or or_1 (or_1_out, and_1_out, reset);
  D_Flip_Flop d_ff_3 (.clk(d_ff_2_qn), .D(d_ff_3_qn), .Q(o2), .Qn(d_ff_3_qn), .reset(or_1_out));  // open: preset, en
  and and_1 (and_1_out, o2, o1);

  assign o3 = 1'b0;

  // Notes on the sheet:
  //   221b307
endmodule

module mod_10 (
  input  clock,
  input  reset,
  output o0,
  output o1,
  output o2,
  output o3
);

  wire and_1_out, d_ff_1_qn, d_ff_2_qn, d_ff_3_qn, d_ff_4_qn, or_1_out;

  D_Flip_Flop d_ff_1 (.clk(clock), .D(d_ff_1_qn), .Q(o0), .Qn(d_ff_1_qn), .reset(or_1_out));  // open: preset, en
  D_Flip_Flop d_ff_2 (.clk(d_ff_1_qn), .D(d_ff_2_qn), .Q(o1), .Qn(d_ff_2_qn), .reset(or_1_out));  // open: preset, en
  or or_1 (or_1_out, and_1_out, reset);
  D_Flip_Flop d_ff_3 (.clk(d_ff_2_qn), .D(d_ff_3_qn), .Q(o2), .Qn(d_ff_3_qn), .reset(or_1_out));  // open: preset, en
  and and_1 (and_1_out, o1, o3);
  D_Flip_Flop d_ff_4 (.clk(d_ff_3_qn), .D(d_ff_4_qn), .Q(o3), .Qn(d_ff_4_qn), .reset(or_1_out));  // open: preset, en

  // Notes on the sheet:
  //   221b307
endmodule
